# Fritzing sketch WoMoStromSpannung (saved by Fritzing 0.9.1b)
circuit board: 8.46667cm x 5.64444cm
breadboards: 1

parts:
  Bauteil1 = Arduino Uno (Rev3)
  LCD1 = LCD screen
  R1 = Rotary Potentiometer (Small) [maximum_resistance=100kΩ package=THT]
  R2 = Resistor [tolerance=±5% resistance=10k package=THT]
  R3 = Resistor [tolerance=±5% resistance=5k package=THT]
  D1 = Zener Diode [part_number=1N4732A breakdown_voltage=5.1V package="300 mil [THT]"]
  ACS714 = ACS714 Stromsensor -5 ... +5A
  Power_plug_12V_in = Power plug
  Power_plug_12V_out = Power plug
  S1 = Pushbutton [package="[THT]"]
  R4 = Resistor [tolerance=±5% resistance=220 package=THT]

nets:
  N1: Bauteil1.A0, R2.Pin_1, R3.Pin_0, D1.cathode
  N2: Bauteil1.A1, ACS714.OUT
  N3: Bauteil1.D11_PWM/MOSI, LCD1.E
  N4: Bauteil1.D12/MISO, LCD1.RS
  N5: Bauteil1.D2, LCD1.DB7
  N6: Bauteil1.D4, LCD1.DB5
  N7: Bauteil1.D5_PWM, LCD1.DB4
  N8: Bauteil1.D6_PWM, LCD1.LED+, R1.leg2
  N9: Bauteil1.D7, S1.Pin_1, S1.Pin_2, R4.Pin_0
  5V: Bauteil1.5V, LCD1.VDD, ACS714.Vcc, S1.Pin_3, S1.Pin_4
  GND: Bauteil1.GND, LCD1.VSS, LCD1.R/W, LCD1.LED-, R1.leg1, R3.Pin_1, D1.anode, ACS714.GND, Power_plug_12V_in.GND, Power_plug_12V_out.GND, R4.Pin_1
  N10: LCD1.V0, R1.wiper
  N11: R2.Pin_0, ACS714.Strom_+_OUT, Power_plug_12V_in.VCC
  N12: ACS714.Strom_+_IN, Power_plug_12V_out.VCC

custom parts:
  ACS714 Stromsensor -5 ... +5A: ACS714 Stromsensor Breakout Board -5 to +5A
